// Logisim project Marina.circ as structural Verilog
module MARINA_8BITS_COMPUTER (
  input  MANUAL_PROGRAMING,
  input  in_2,
  input  in_3,
  input  PROGRAM_MODE,
  input  in_5,
  input  in_6,
  input  in_7,
  input  in_8,
  input  in_9,
  input  in_10,
  input  in_11,
  input  in_12,
  input  in_13,
  input  in_14,
  input  in_15,
  input  in_16,
  input  in_17,
  input  in_18,
  input  in_19,
  input  in_20,
  input  in_21,
  input  in_22,
  input  in_23,
  input  in_24,
  input  in_25,
  input  in_26,
  input  in_27,
  input  in_28,
  output out_29,
  output out_30
);

  wire AI, AO, B_CLK, BI, BO, CE, CLK, clock_1_out, CO, controlled_buffer_1_out, controlled_buffer_2_out,
       controlled_buffer_3_out, controlled_buffer_4_out, controlled_buffer_5_out, controlled_buffer_6_out,
       controlled_buffer_7_out, controlled_buffer_8_out, EO, FI, HL, II, instrucion_register_1_l0,
       instrucion_register_1_l1, instrucion_register_1_l2, instrucion_register_1_l3,
       instrucion_register_1_l4, instrucion_register_1_l5, instrucion_register_1_l6,
       instrucion_register_1_l7, IO, JP, mar_1_l0, mar_1_l1, mar_1_l2, mar_1_l3, mar_1_l4, mar_1_l5,
       mar_1_l6, mar_1_l7, mar_1_l8, mar_1_l9, mar_1_la, mar_1_lb, mar_1_lc, mar_1_ld, mar_1_le, mar_1_lf,
       MI, OI, or_1_out, or_2_out, program_counter_1_l0, program_counter_1_l1, program_counter_1_l2,
       program_counter_1_l3, program_counter_1_l4, program_counter_1_l5, program_counter_1_l6,
       program_counter_1_l7, REST, RI, RO, SU;
  wire [7:0] ram_1_dout, undriven;
  wire [15:0] mar_1_addrs;

  or or_1 (or_1_out, RO, CLK);
  RAM #(.addrWidth(16)) ram_1 (.addr(mar_1_addrs), .we(RI), .oe(RO), .clk(or_1_out), .din(undriven), .dout(ram_1_dout));
  Clock clock_1 (.out(clock_1_out));
  MAR mar_1 (
    .ENABLE(1'b1), .I0(controlled_buffer_1_out), .I1(controlled_buffer_2_out), .I2(controlled_buffer_3_out),
    .I3(controlled_buffer_4_out), .CLOCK(CLK), .LOAD(MI), .RESET(REST), .L0(mar_1_l0), .L1(mar_1_l1),
    .L2(mar_1_l2), .L3(mar_1_l3), .L4(mar_1_l4), .L5(mar_1_l5), .L6(mar_1_l6), .L7(mar_1_l7), .L8(mar_1_l8),
    .L9(mar_1_l9), .LA(mar_1_la), .LB(mar_1_lb), .LC(mar_1_lc), .LD(mar_1_ld), .LE(mar_1_le), .LF(mar_1_lf),
    .ADDRS(mar_1_addrs));  // open: I4, I5, I6, I7
  DotMatrix #(.matrixcols(16), .matrixrows(1)) dotmatrix_1 (
    .col0(mar_1_l0), .col1(mar_1_l1), .col2(mar_1_l2), .col3(mar_1_l3), .col4(mar_1_l4), .col5(mar_1_l5),
    .col6(mar_1_l6), .col7(mar_1_l7), .col8(mar_1_l8), .col9(mar_1_l9), .col10(mar_1_la), .col11(mar_1_lb),
    .col12(mar_1_lc), .col13(mar_1_ld), .col14(mar_1_le), .col15(mar_1_lf));
  DotMatrix #(.matrixcols(4), .matrixrows(1)) dotmatrix_2 (
    .col0(instrucion_register_1_l7), .col1(instrucion_register_1_l6), .col2(instrucion_register_1_l5),
    .col3(instrucion_register_1_l4));
  or or_2 (or_2_out, clock_1_out, B_CLK);
  INSTRUCION_REGISTER instrucion_register_1 (
    .ENABLE(IO), .I0(controlled_buffer_1_out), .I1(controlled_buffer_2_out), .I2(controlled_buffer_3_out),
    .I3(controlled_buffer_4_out), .I4(controlled_buffer_5_out), .I5(controlled_buffer_6_out),
    .I6(controlled_buffer_7_out), .I7(controlled_buffer_8_out), .CLOCK(CLK), .LOAD(II), .RESET(REST),
    .L0(instrucion_register_1_l0), .L1(instrucion_register_1_l1), .L2(instrucion_register_1_l2),
    .L3(instrucion_register_1_l3), .L4(instrucion_register_1_l4), .L5(instrucion_register_1_l5),
    .L6(instrucion_register_1_l6), .L7(instrucion_register_1_l7));  // open: O0, O1, O2, O3, O4, O5, O6, O7
  DotMatrix #(.matrixcols(4), .matrixrows(1)) dotmatrix_3 (
    .col0(instrucion_register_1_l3), .col1(instrucion_register_1_l2), .col2(instrucion_register_1_l1),
    .col3(instrucion_register_1_l0));
  Button CLCK (.out(B_CLK));
  Button RESET (.out(REST));
  DotMatrix #(.matrixcols(4), .matrixrows(1)) dotmatrix_4 (
    .col0(controlled_buffer_4_out), .col1(controlled_buffer_3_out), .col2(controlled_buffer_2_out),
    .col3(controlled_buffer_1_out));
  assign controlled_buffer_1_out = in_12 ? in_21 : 1'bz;  // Controlled_Buffer controlled_buffer_1
  assign controlled_buffer_2_out = in_12 ? in_20 : 1'bz;  // Controlled_Buffer controlled_buffer_2
  assign controlled_buffer_3_out = in_12 ? in_19 : 1'bz;  // Controlled_Buffer controlled_buffer_3
  assign controlled_buffer_4_out = in_12 ? in_18 : 1'bz;  // Controlled_Buffer controlled_buffer_4
  assign controlled_buffer_5_out = in_12 ? in_17 : 1'bz;  // Controlled_Buffer controlled_buffer_5
  assign controlled_buffer_6_out = in_12 ? in_16 : 1'bz;  // Controlled_Buffer controlled_buffer_6
  assign controlled_buffer_7_out = in_12 ? in_15 : 1'bz;  // Controlled_Buffer controlled_buffer_7
  assign controlled_buffer_8_out = in_12 ? in_14 : 1'bz;  // Controlled_Buffer controlled_buffer_8
  and and_1 (CLK, or_2_out, ~HL);  // AND_Gate
  assign controlled_buffer_1_out = RO ? ram_1_dout[0] : 1'bz;  // Controlled_Buffer controlled_buffer_9
  assign controlled_buffer_2_out = RO ? ram_1_dout[1] : 1'bz;  // Controlled_Buffer controlled_buffer_10
  assign controlled_buffer_3_out = RO ? ram_1_dout[2] : 1'bz;  // Controlled_Buffer controlled_buffer_11
  assign controlled_buffer_4_out = RO ? ram_1_dout[3] : 1'bz;  // Controlled_Buffer controlled_buffer_12
  assign controlled_buffer_5_out = RO ? ram_1_dout[4] : 1'bz;  // Controlled_Buffer controlled_buffer_13
  assign controlled_buffer_6_out = RO ? ram_1_dout[5] : 1'bz;  // Controlled_Buffer controlled_buffer_14
  assign controlled_buffer_7_out = RO ? ram_1_dout[6] : 1'bz;  // Controlled_Buffer controlled_buffer_15
  assign controlled_buffer_8_out = RO ? ram_1_dout[7] : 1'bz;  // Controlled_Buffer controlled_buffer_16
  DotMatrix #(.matrixcols(8), .matrixrows(1)) dotmatrix_5 (
    .col0(controlled_buffer_8_out), .col1(controlled_buffer_7_out), .col2(controlled_buffer_6_out),
    .col3(controlled_buffer_5_out), .col4(controlled_buffer_4_out), .col5(controlled_buffer_3_out),
    .col6(controlled_buffer_2_out), .col7(controlled_buffer_1_out));
  assign MI = MANUAL_PROGRAMING ? in_2 : 1'bz;  // Controlled_Buffer controlled_buffer_17
  assign RI = MANUAL_PROGRAMING ? in_6 : 1'bz;  // Controlled_Buffer controlled_buffer_18
  assign RO = MANUAL_PROGRAMING ? in_8 : 1'bz;  // Controlled_Buffer controlled_buffer_19
  assign II = MANUAL_PROGRAMING ? in_9 : 1'bz;  // Controlled_Buffer controlled_buffer_20
  assign IO = MANUAL_PROGRAMING ? in_10 : 1'bz;  // Controlled_Buffer controlled_buffer_21
  assign OI = MANUAL_PROGRAMING ? in_13 : 1'bz;  // Controlled_Buffer controlled_buffer_22
  assign BI = MANUAL_PROGRAMING ? in_23 : 1'bz;  // Controlled_Buffer controlled_buffer_23
  assign BO = MANUAL_PROGRAMING ? in_25 : 1'bz;  // Controlled_Buffer controlled_buffer_24
  PROGRAM_COUNTER program_counter_1 (
    .COut(CO), .CEnable(CE), .CWrite(JP), .CReset(REST), .CLOCK(CLK), .I3(controlled_buffer_4_out),
    .I2(controlled_buffer_3_out), .I1(controlled_buffer_2_out), .I0(controlled_buffer_1_out),
    .O3(controlled_buffer_4_out), .O2(controlled_buffer_3_out), .O1(controlled_buffer_2_out),
    .O0(controlled_buffer_1_out), .L7(program_counter_1_l7), .L6(program_counter_1_l6),
    .L5(program_counter_1_l5), .L4(program_counter_1_l4), .L3(program_counter_1_l3),
    .L2(program_counter_1_l2), .L1(program_counter_1_l1), .L0(program_counter_1_l0));  // open: I7, I6, I5, I4, O7, O6, O5, O4
  DotMatrix #(.matrixcols(8), .matrixrows(1)) dotmatrix_6 (
    .col0(program_counter_1_l0), .col1(program_counter_1_l1), .col2(program_counter_1_l2),
    .col3(program_counter_1_l3), .col4(program_counter_1_l4), .col5(program_counter_1_l5),
    .col6(program_counter_1_l6), .col7(program_counter_1_l7));
  A_REGISTER a_register_1 (
    .ENABLE(AO), .CLOCK(CLK), .LOAD(AI), .RESET(REST));  // open: I0, I1, I2, I3, I4, I5, I6, I7, O0, O1, O2, O3, O4, O5, O6, O7, L0, L1, L2, L3, L4, L5, L6, L7
  B_REGISTER b_register_1 (
    .ENABLE(BO), .CLOCK(CLK), .LOAD(BI), .RESET(REST));  // open: I0, I1, I2, I3, I4, I5, I6, I7, O0, O1, O2, O3, O4, O5, O6, O7, L0, L1, L2, L3, L4, L5, L6, L7
  assign CO = MANUAL_PROGRAMING ? in_3 : 1'bz;  // Controlled_Buffer controlled_buffer_25
  assign JP = MANUAL_PROGRAMING ? in_5 : 1'bz;  // Controlled_Buffer controlled_buffer_26
  assign CE = MANUAL_PROGRAMING ? in_7 : 1'bz;  // Controlled_Buffer controlled_buffer_27
  assign SU = MANUAL_PROGRAMING ? in_11 : 1'bz;  // Controlled_Buffer controlled_buffer_28
  assign EO = MANUAL_PROGRAMING ? in_22 : 1'bz;  // Controlled_Buffer controlled_buffer_29
  assign AI = MANUAL_PROGRAMING ? in_24 : 1'bz;  // Controlled_Buffer controlled_buffer_30
  assign AO = MANUAL_PROGRAMING ? in_26 : 1'bz;  // Controlled_Buffer controlled_buffer_31
  assign FI = MANUAL_PROGRAMING ? in_27 : 1'bz;  // Controlled_Buffer controlled_buffer_32
  assign HL = MANUAL_PROGRAMING ? in_28 : 1'bz;  // Controlled_Buffer controlled_buffer_33

  // Other names for the same wires on the sheet: CF = out_29; ZF = out_30
endmodule

module PROGRAM_COUNTER (
  input  COut,
  input  CEnable,
  input  CWrite,
  input  CReset,
  input  CLOCK,
  input  I7,
  input  I6,
  input  I5,
  input  I4,
  input  I3,
  input  I2,
  input  I1,
  input  I0,
  output O7,
  output O6,
  output O5,
  output O4,
  output O3,
  output O2,
  output O1,
  output O0,
  output L7,
  output L6,
  output L5,
  output L4,
  output L3,
  output L2,
  output L1,
  output L0
);

  wire and_1_out, and_2_out, and_3_out, and_4_out, and_5_out, and_6_out, and_7_out, and_8_out, and_9_out,
       and_10_out, and_11_out, and_12_out, and_13_out, and_14_out, and_15_out, and_16_out, j_k_ff_2_qn,
       j_k_ff_3_qn, j_k_ff_4_qn, j_k_ff_5_qn, j_k_ff_6_qn, j_k_ff_7_qn, j_k_ff_8_qn, or_1_out, or_2_out,
       or_3_out, or_4_out, or_5_out, or_6_out, or_7_out, or_8_out;

  J_K_Flip_Flop j_k_ff_1 (
    .J(CEnable), .K(CEnable), .clk(j_k_ff_2_qn), .Q(L7), .preset(and_1_out), .reset(or_1_out));  // open: Qn
  or or_1 (or_1_out, CReset, and_2_out);
  and and_1 (and_1_out, CWrite, I7, CLOCK);
  and and_2 (and_2_out, CWrite, ~I7, CLOCK);  // AND_Gate
  J_K_Flip_Flop j_k_ff_2 (
    .J(CEnable), .K(CEnable), .clk(j_k_ff_3_qn), .Q(L6), .Qn(j_k_ff_2_qn), .preset(and_3_out),
    .reset(or_2_out));
  or or_2 (or_2_out, CReset, and_4_out);
  and and_3 (and_3_out, CWrite, I6, CLOCK);
  and and_4 (and_4_out, CWrite, ~I6, CLOCK);  // AND_Gate
  assign O7 = COut ? L7 : 1'bz;  // Controlled_Buffer controlled_buffer_1
  assign O6 = COut ? L6 : 1'bz;  // Controlled_Buffer controlled_buffer_2
  J_K_Flip_Flop j_k_ff_3 (
    .J(CEnable), .K(CEnable), .clk(j_k_ff_4_qn), .Q(L5), .Qn(j_k_ff_3_qn), .preset(and_5_out),
    .reset(or_3_out));
  or or_3 (or_3_out, CReset, and_6_out);
  and and_5 (and_5_out, CWrite, I5, CLOCK);
  and and_6 (and_6_out, CWrite, ~I5, CLOCK);  // AND_Gate
  assign O5 = COut ? L5 : 1'bz;  // Controlled_Buffer controlled_buffer_3
  assign O4 = COut ? L4 : 1'bz;  // Controlled_Buffer controlled_buffer_4
  assign O3 = COut ? L3 : 1'bz;  // Controlled_Buffer controlled_buffer_5
  assign O2 = COut ? L2 : 1'bz;  // Controlled_Buffer controlled_buffer_6
  J_K_Flip_Flop j_k_ff_4 (
    .J(CEnable), .K(CEnable), .clk(j_k_ff_5_qn), .Q(L4), .Qn(j_k_ff_4_qn), .preset(and_7_out),
    .reset(or_4_out));
  or or_4 (or_4_out, CReset, and_8_out);
  and and_7 (and_7_out, CWrite, I4, CLOCK);
  and and_8 (and_8_out, CWrite, ~I4, CLOCK);  // AND_Gate
  assign O1 = COut ? L1 : 1'bz;  // Controlled_Buffer controlled_buffer_7
  assign O0 = COut ? L0 : 1'bz;  // Controlled_Buffer controlled_buffer_8
  J_K_Flip_Flop j_k_ff_5 (
    .J(CEnable), .K(CEnable), .clk(j_k_ff_6_qn), .Q(L3), .Qn(j_k_ff_5_qn), .preset(and_9_out),
    .reset(or_5_out));
  or or_5 (or_5_out, CReset, and_10_out);
  and and_9 (and_9_out, CWrite, I3, CLOCK);
  J_K_Flip_Flop j_k_ff_6 (
    .J(CEnable), .K(CEnable), .clk(j_k_ff_7_qn), .Q(L2), .Qn(j_k_ff_6_qn), .preset(and_11_out),
    .reset(or_6_out));
  and and_10 (and_10_out, CWrite, ~I3, CLOCK);  // AND_Gate
  and and_11 (and_11_out, CWrite, I2, CLOCK);
  J_K_Flip_Flop j_k_ff_7 (
    .J(CEnable), .K(CEnable), .clk(j_k_ff_8_qn), .Q(L1), .Qn(j_k_ff_7_qn), .preset(and_13_out),
    .reset(or_7_out));
  or or_6 (or_6_out, CReset, and_12_out);
  and and_12 (and_12_out, CWrite, ~I2, CLOCK);  // AND_Gate
  and and_13 (and_13_out, CWrite, I1, CLOCK);
  or or_7 (or_7_out, CReset, and_15_out);
  and and_14 (and_14_out, CWrite, I0, CLOCK);
  and and_15 (and_15_out, CWrite, ~I1, CLOCK);  // AND_Gate
  J_K_Flip_Flop j_k_ff_8 (
    .J(CEnable), .K(CEnable), .clk(CLOCK), .Q(L0), .Qn(j_k_ff_8_qn), .preset(and_14_out), .reset(or_8_out));
  or or_8 (or_8_out, CReset, and_16_out);
  and and_16 (and_16_out, CWrite, ~I0, CLOCK);  // AND_Gate
endmodule

module MAR (
  input  CLOCK,
  input  LOAD,
  input  RESET,
  input  ENABLE,
  input  I0,
  input  I1,
  input  I2,
  input  I3,
  input  I4,
  input  I5,
  input  I6,
  input  I7,
  output L0,
  output L1,
  output L2,
  output L3,
  output L4,
  output L5,
  output L6,
  output L7,
  output L8,
  output L9,
  output LA,
  output LB,
  output LC,
  output LD,
  output LE,
  output LF,
  output [15:0] ADDRS
);

  wire register_1_q, register_2_q, register_3_q, register_4_q, register_5_q, register_6_q, register_7_q,
       register_8_q;

  Register #(.width(1)) register_1 (.D(I0), .en(LOAD), .clk(CLOCK), .Q(register_1_q), .clr(RESET));
  Register #(.width(1)) register_2 (.D(I1), .en(LOAD), .clk(CLOCK), .Q(register_2_q), .clr(RESET));
  Register #(.width(1)) register_3 (.D(I2), .en(LOAD), .clk(CLOCK), .Q(register_3_q), .clr(RESET));
  Register #(.width(1)) register_4 (.D(I3), .en(LOAD), .clk(CLOCK), .Q(register_4_q), .clr(RESET));
  Register #(.width(1)) register_5 (.D(I4), .en(LOAD), .clk(CLOCK), .Q(register_5_q), .clr(RESET));
  Register #(.width(1)) register_6 (.D(I5), .en(LOAD), .clk(CLOCK), .Q(register_6_q), .clr(RESET));
  Register #(.width(1)) register_7 (.D(I6), .en(LOAD), .clk(CLOCK), .Q(register_7_q), .clr(RESET));
  Register #(.width(1)) register_8 (.D(I7), .en(LOAD), .clk(CLOCK), .Q(register_8_q), .clr(RESET));
  DECODER_4BITS decoder_4bits_1 (
    .I3(register_4_q), .I2(register_3_q), .I1(register_2_q), .I0(register_1_q), .ENABLE(1'b1), .DF(LF),
    .DE(LE), .DD(LD), .DC(LC), .DB(LB), .DA(LA), .D9(L9), .D8(L8), .D7(L7), .D6(L6), .D5(L5), .D4(L4),
    .D3(L3), .D2(L2), .D1(L1), .D0(L0));
  assign ADDRS[4] = ENABLE ? L4 : 1'bz;  // Controlled_Buffer controlled_buffer_1
  assign ADDRS[5] = ENABLE ? L5 : 1'bz;  // Controlled_Buffer controlled_buffer_2
  assign ADDRS[6] = ENABLE ? L6 : 1'bz;  // Controlled_Buffer controlled_buffer_3
  assign ADDRS[7] = ENABLE ? L7 : 1'bz;  // Controlled_Buffer controlled_buffer_4
  assign ADDRS[12] = ENABLE ? LC : 1'bz;  // Controlled_Buffer controlled_buffer_5
  assign ADDRS[13] = ENABLE ? LD : 1'bz;  // Controlled_Buffer controlled_buffer_6
  assign ADDRS[14] = ENABLE ? LE : 1'bz;  // Controlled_Buffer controlled_buffer_7
  assign ADDRS[15] = ENABLE ? LF : 1'bz;  // Controlled_Buffer controlled_buffer_8
  assign ADDRS[0] = ENABLE ? L0 : 1'bz;  // Controlled_Buffer controlled_buffer_9
  assign ADDRS[1] = ENABLE ? L1 : 1'bz;  // Controlled_Buffer controlled_buffer_10
  assign ADDRS[2] = ENABLE ? L2 : 1'bz;  // Controlled_Buffer controlled_buffer_11
  assign ADDRS[3] = ENABLE ? L3 : 1'bz;  // Controlled_Buffer controlled_buffer_12
  assign ADDRS[8] = ENABLE ? L8 : 1'bz;  // Controlled_Buffer controlled_buffer_13
  assign ADDRS[9] = ENABLE ? L9 : 1'bz;  // Controlled_Buffer controlled_buffer_14
  assign ADDRS[10] = ENABLE ? LA : 1'bz;  // Controlled_Buffer controlled_buffer_15
  assign ADDRS[11] = ENABLE ? LB : 1'bz;  // Controlled_Buffer controlled_buffer_16
endmodule

module DECODER_4BITS (
  input  ENABLE,
  input  I3,
  input  I2,
  input  I1,
  input  I0,
  output DF,
  output DE,
  output DD,
  output DC,
  output DB,
  output DA,
  output D9,
  output D8,
  output D7,
  output D6,
  output D5,
  output D4,
  output D3,
  output D2,
  output D1,
  output D0
);

  wire and_1_out, and_2_out, and_3_out, and_4_out, and_5_out, and_6_out, and_7_out, and_8_out, and_9_out,
       and_10_out, and_11_out, and_12_out, and_13_out, and_14_out, and_15_out, and_16_out, not_1_out,
       not_2_out, not_3_out, not_4_out;

  not not_1 (not_1_out, I3);
  not not_2 (not_2_out, I2);
  not not_3 (not_3_out, I1);
  not not_4 (not_4_out, I0);
  and and_1 (and_1_out, not_1_out, not_2_out, not_3_out, not_4_out);
  and and_2 (and_2_out, not_1_out, not_2_out, not_3_out, I0);
  and and_3 (and_3_out, not_1_out, not_2_out, I1, not_4_out);
  and and_4 (and_4_out, not_1_out, not_2_out, I1, I0);
  and and_5 (and_5_out, not_1_out, I2, not_3_out, not_4_out);
  and and_6 (and_6_out, not_1_out, I2, not_3_out, I0);
  and and_7 (and_7_out, not_1_out, I2, I1, not_4_out);
  and and_8 (and_8_out, not_1_out, I2, I1, I0);
  and and_9 (and_9_out, I3, not_2_out, not_3_out, not_4_out);
  and and_10 (and_10_out, I3, not_2_out, not_3_out, I0);
  and and_11 (and_11_out, I3, not_2_out, I1, not_4_out);
  and and_12 (and_12_out, I3, not_2_out, I1, I0);
  and and_13 (and_13_out, I3, I2, not_3_out, not_4_out);
  and and_14 (and_14_out, I3, I2, not_3_out, I0);
  and and_15 (and_15_out, I3, I2, I1, not_4_out);
  and and_16 (and_16_out, I3, I2, I1, I0);
  assign DF = ENABLE ? and_16_out : 1'bz;  // Controlled_Buffer controlled_buffer_1
  assign DE = ENABLE ? and_15_out : 1'bz;  // Controlled_Buffer controlled_buffer_2
  assign DD = ENABLE ? and_14_out : 1'bz;  // Controlled_Buffer controlled_buffer_3
  assign DC = ENABLE ? and_13_out : 1'bz;  // Controlled_Buffer controlled_buffer_4
  assign DB = ENABLE ? and_12_out : 1'bz;  // Controlled_Buffer controlled_buffer_5
  assign DA = ENABLE ? and_11_out : 1'bz;  // Controlled_Buffer controlled_buffer_6
  assign D9 = ENABLE ? and_10_out : 1'bz;  // Controlled_Buffer controlled_buffer_7
  assign D8 = ENABLE ? and_9_out : 1'bz;  // Controlled_Buffer controlled_buffer_8
  assign D7 = ENABLE ? and_8_out : 1'bz;  // Controlled_Buffer controlled_buffer_9
  assign D6 = ENABLE ? and_7_out : 1'bz;  // Controlled_Buffer controlled_buffer_10
  assign D5 = ENABLE ? and_6_out : 1'bz;  // Controlled_Buffer controlled_buffer_11
  assign D4 = ENABLE ? and_5_out : 1'bz;  // Controlled_Buffer controlled_buffer_12
  assign D3 = ENABLE ? and_4_out : 1'bz;  // Controlled_Buffer controlled_buffer_13
  assign D2 = ENABLE ? and_3_out : 1'bz;  // Controlled_Buffer controlled_buffer_14
  assign D1 = ENABLE ? and_2_out : 1'bz;  // Controlled_Buffer controlled_buffer_15
  assign D0 = ENABLE ? and_1_out : 1'bz;  // Controlled_Buffer controlled_buffer_16
endmodule

module A_REGISTER (
  input  CLOCK,
  input  LOAD,
  input  RESET,
  input  ENABLE,
  input  I0,
  input  I1,
  input  I2,
  input  I3,
  input  I4,
  input  I5,
  input  I6,
  input  I7,
  output L0,
  output L1,
  output L2,
  output L3,
  output L4,
  output L5,
  output L6,
  output L7,
  output O0,
  output O1,
  output O2,
  output O3,
  output O4,
  output O5,
  output O6,
  output O7
);

  Register #(.width(1)) register_1 (.D(I0), .en(LOAD), .clk(CLOCK), .Q(L0), .clr(RESET));
  Register #(.width(1)) register_2 (.D(I1), .en(LOAD), .clk(CLOCK), .Q(L1), .clr(RESET));
  Register #(.width(1)) register_3 (.D(I2), .en(LOAD), .clk(CLOCK), .Q(L2), .clr(RESET));
  Register #(.width(1)) register_4 (.D(I3), .en(LOAD), .clk(CLOCK), .Q(L3), .clr(RESET));
  Register #(.width(1)) register_5 (.D(I4), .en(LOAD), .clk(CLOCK), .Q(L4), .clr(RESET));
  Register #(.width(1)) register_6 (.D(I5), .en(LOAD), .clk(CLOCK), .Q(L5), .clr(RESET));
  Register #(.width(1)) register_7 (.D(I6), .en(LOAD), .clk(CLOCK), .Q(L6), .clr(RESET));
  Register #(.width(1)) register_8 (.D(I7), .en(LOAD), .clk(CLOCK), .Q(L7), .clr(RESET));
  assign O6 = ENABLE ? L6 : 1'bz;  // Controlled_Buffer controlled_buffer_1
  assign O7 = ENABLE ? L7 : 1'bz;  // Controlled_Buffer controlled_buffer_2
  assign O2 = ENABLE ? L2 : 1'bz;  // Controlled_Buffer controlled_buffer_3
  assign O3 = ENABLE ? L3 : 1'bz;  // Controlled_Buffer controlled_buffer_4
  assign O4 = ENABLE ? L4 : 1'bz;  // Controlled_Buffer controlled_buffer_5
  assign O5 = ENABLE ? L5 : 1'bz;  // Controlled_Buffer controlled_buffer_6
  assign O0 = ENABLE ? L0 : 1'bz;  // Controlled_Buffer controlled_buffer_7
  assign O1 = ENABLE ? L1 : 1'bz;  // Controlled_Buffer controlled_buffer_8
endmodule

module INSTRUCION_REGISTER (
  input  CLOCK,
  input  LOAD,
  input  RESET,
  input  ENABLE,
  input  I0,
  input  I1,
  input  I2,
  input  I3,
  input  I4,
  input  I5,
  input  I6,
  input  I7,
  output L0,
  output L1,
  output L2,
  output L3,
  output L4,
  output L5,
  output L6,
  output L7,
  output O0,
  output O1,
  output O2,
  output O3,
  output O4,
  output O5,
  output O6,
  output O7
);

  Register #(.width(1)) register_1 (.D(I0), .en(LOAD), .clk(CLOCK), .Q(L0), .clr(RESET));
  Register #(.width(1)) register_2 (.D(I1), .en(LOAD), .clk(CLOCK), .Q(L1), .clr(RESET));
  Register #(.width(1)) register_3 (.D(I2), .en(LOAD), .clk(CLOCK), .Q(L2), .clr(RESET));
  Register #(.width(1)) register_4 (.D(I3), .en(LOAD), .clk(CLOCK), .Q(L3), .clr(RESET));
  Register #(.width(1)) register_5 (.D(I4), .en(LOAD), .clk(CLOCK), .Q(L4), .clr(RESET));
  Register #(.width(1)) register_6 (.D(I5), .en(LOAD), .clk(CLOCK), .Q(L5), .clr(RESET));
  Register #(.width(1)) register_7 (.D(I6), .en(LOAD), .clk(CLOCK), .Q(L6), .clr(RESET));
  Register #(.width(1)) register_8 (.D(I7), .en(LOAD), .clk(CLOCK), .Q(L7), .clr(RESET));
  assign O5 = ENABLE ? L5 : 1'bz;  // Controlled_Buffer controlled_buffer_1
  assign O6 = ENABLE ? L6 : 1'bz;  // Controlled_Buffer controlled_buffer_2
  assign O7 = ENABLE ? L7 : 1'bz;  // Controlled_Buffer controlled_buffer_3
  assign O1 = ENABLE ? L1 : 1'bz;  // Controlled_Buffer controlled_buffer_4
  assign O2 = ENABLE ? L2 : 1'bz;  // Controlled_Buffer controlled_buffer_5
  assign O3 = ENABLE ? L3 : 1'bz;  // Controlled_Buffer controlled_buffer_6
  assign O4 = ENABLE ? L4 : 1'bz;  // Controlled_Buffer controlled_buffer_7
  assign O0 = ENABLE ? L0 : 1'bz;  // Controlled_Buffer controlled_buffer_8
endmodule

module B_REGISTER (
  input  CLOCK,
  input  LOAD,
  input  RESET,
  input  ENABLE,
  input  I0,
  input  I1,
  input  I2,
  input  I3,
  input  I4,
  input  I5,
  input  I6,
  input  I7,
  output L0,
  output L1,
  output L2,
  output L3,
  output L4,
  output L5,
  output L6,
  output L7,
  output O0,
  output O1,
  output O2,
  output O3,
  output O4,
  output O5,
  output O6,
  output O7
);

  Register #(.width(1)) register_1 (.D(I0), .en(LOAD), .clk(CLOCK), .Q(L0), .clr(RESET));
  Register #(.width(1)) register_2 (.D(I1), .en(LOAD), .clk(CLOCK), .Q(L1), .clr(RESET));
  Register #(.width(1)) register_3 (.D(I2), .en(LOAD), .clk(CLOCK), .Q(L2), .clr(RESET));
  Register #(.width(1)) register_4 (.D(I3), .en(LOAD), .clk(CLOCK), .Q(L3), .clr(RESET));
  Register #(.width(1)) register_5 (.D(I4), .en(LOAD), .clk(CLOCK), .Q(L4), .clr(RESET));
  Register #(.width(1)) register_6 (.D(I5), .en(LOAD), .clk(CLOCK), .Q(L5), .clr(RESET));
  Register #(.width(1)) register_7 (.D(I6), .en(LOAD), .clk(CLOCK), .Q(L6), .clr(RESET));
  Register #(.width(1)) register_8 (.D(I7), .en(LOAD), .clk(CLOCK), .Q(L7), .clr(RESET));
  assign O6 = ENABLE ? L6 : 1'bz;  // Controlled_Buffer controlled_buffer_1
  assign O7 = ENABLE ? L7 : 1'bz;  // Controlled_Buffer controlled_buffer_2
  assign O2 = ENABLE ? L2 : 1'bz;  // Controlled_Buffer controlled_buffer_3
  assign O3 = ENABLE ? L3 : 1'bz;  // Controlled_Buffer controlled_buffer_4
  assign O4 = ENABLE ? L4 : 1'bz;  // Controlled_Buffer controlled_buffer_5
  assign O5 = ENABLE ? L5 : 1'bz;  // Controlled_Buffer controlled_buffer_6
  assign O0 = ENABLE ? L0 : 1'bz;  // Controlled_Buffer controlled_buffer_7
  assign O1 = ENABLE ? L1 : 1'bz;  // Controlled_Buffer controlled_buffer_8
endmodule
