// Logisim project examples.circ as structural Verilog
module bus_and_rgisters (
  input  in_1,
  input  in_2,
  input  in_3,
  input  in_4,
  input  in_5,
  input  in_6,
  input  in_7,
  input  in_8,
  input  in_9,
  input  in_10,
  input  in_11,
  output out_12,
  output out_13,
  output out_14,
  output out_15,
  output out_16,
  output out_17,
  output out_18,
  output out_19,
  output out_20,
  output out_21
);

  wire clock_1_out, j_k_ff_1_q, j_k_ff_2_q, j_k_ff_3_q, j_k_ff_4_q, j_k_ff_5_q, j_k_ff_6_q, j_k_ff_7_q,
       j_k_ff_8_q;
  wire [7:0] j_k_ff_1_qn;

  Clock clock_1 (.out(clock_1_out));
  J_K_Flip_Flop j_k_ff_1 (
    .J(clock_1_out), .K(clock_1_out), .clk(clock_1_out), .Q(j_k_ff_1_q), .Qn(j_k_ff_1_qn[0]), .reset(in_7));  // open: preset
  J_K_Flip_Flop j_k_ff_2 (
    .J(j_k_ff_1_q), .K(j_k_ff_1_q), .clk(j_k_ff_1_q), .Q(j_k_ff_2_q), .Qn(j_k_ff_1_qn[1]), .reset(in_7));  // open: preset
  J_K_Flip_Flop j_k_ff_3 (
    .J(j_k_ff_2_q), .K(j_k_ff_2_q), .clk(j_k_ff_2_q), .Q(j_k_ff_3_q), .Qn(j_k_ff_1_qn[2]), .reset(in_7));  // open: preset
  J_K_Flip_Flop j_k_ff_4 (
    .J(j_k_ff_3_q), .K(j_k_ff_3_q), .clk(j_k_ff_3_q), .Q(j_k_ff_4_q), .Qn(j_k_ff_1_qn[3]), .reset(in_7));  // open: preset
  J_K_Flip_Flop j_k_ff_5 (
    .J(j_k_ff_4_q), .K(j_k_ff_4_q), .clk(j_k_ff_4_q), .Q(j_k_ff_5_q), .Qn(j_k_ff_1_qn[4]), .reset(in_7));  // open: preset
  J_K_Flip_Flop j_k_ff_6 (
    .J(j_k_ff_5_q), .K(j_k_ff_5_q), .clk(j_k_ff_5_q), .Q(j_k_ff_6_q), .Qn(j_k_ff_1_qn[5]), .reset(in_7));  // open: preset
  J_K_Flip_Flop j_k_ff_7 (
    .J(j_k_ff_6_q), .K(j_k_ff_6_q), .clk(j_k_ff_6_q), .Q(j_k_ff_7_q), .Qn(j_k_ff_1_qn[6]), .reset(in_7));  // open: preset
  J_K_Flip_Flop j_k_ff_8 (
    .J(j_k_ff_7_q), .K(j_k_ff_7_q), .clk(j_k_ff_7_q), .Q(j_k_ff_8_q), .Qn(j_k_ff_1_qn[7]), .reset(in_7));  // open: preset
  DotMatrix #(.matrixcols(8), .matrixrows(1)) dotmatrix_1 (
    .col0(j_k_ff_1_qn[7]), .col1(j_k_ff_1_qn[6]), .col2(j_k_ff_1_qn[5]), .col3(j_k_ff_1_qn[4]),
    .col4(j_k_ff_1_qn[3]), .col5(j_k_ff_1_qn[2]), .col6(j_k_ff_1_qn[1]), .col7(j_k_ff_1_qn[0]));
  ROM rom_1 ();  // open: addr, data
  RAM ram_1 (.addr(j_k_ff_1_qn));  // open: we, oe, clk, din, dout
  Adder adder_1 (
    .a(j_k_ff_1_qn), .b(j_k_ff_1_qn), .out({out_21, out_20, out_19, out_18, out_17, out_16, out_15, out_14}));  // open: cin, cout
  T_Flip_Flop t_ff_1 ();  // open: T, clk, Q, Qn, reset, preset
  D_Flip_Flop d_ff_1 ();  // open: D, clk, Q, Qn, preset, reset
  J_K_Flip_Flop j_k_ff_9 (.J(in_2), .K(in_3), .clk(in_4), .Q(out_12), .Qn(out_13), .preset(in_1), .reset(in_5));
  S_R_Flip_Flop s_r_ff_1 (.S(in_8), .R(in_9), .clk(in_10), .reset(in_11), .preset(in_6));  // open: Q, Qn
endmodule

module counterr (
);

  PROGRAM_COUNTER program_counter_1 ();  // open: COut, CEnable, CWrite, CReset, CLOCK, I7, I6, I5, I4, I3, I2, I1, I0, O7, O6, O5, O4, O3, O2, O1, O0, L7, L6, L5, L4, L3, L2, L1, L0
endmodule

module registro_8bit (
  input  CLOCK,
  input  LOAD,
  input  RESET,
  input  ENABLE,
  input  I0,
  input  I1,
  input  I2,
  input  I3,
  input  I4,
  input  I5,
  input  I6,
  input  I7,
  output L0,
  output L1,
  output L2,
  output L3,
  output L4,
  output L5,
  output L6,
  output L7,
  output O0,
  output O1,
  output O2,
  output O3,
  output O4,
  output O5,
  output O6,
  output O7
);

  Register #(.width(1)) register_1 (.D(I0), .en(LOAD), .clk(CLOCK), .Q(L0), .clr(RESET));
  Register #(.width(1)) register_2 (.D(I1), .en(LOAD), .clk(CLOCK), .Q(L1), .clr(RESET));
  Register #(.width(1)) register_3 (.D(I2), .en(LOAD), .clk(CLOCK), .Q(L2), .clr(RESET));
  Register #(.width(1)) register_4 (.D(I3), .en(LOAD), .clk(CLOCK), .Q(L3), .clr(RESET));
  Register #(.width(1)) register_5 (.D(I4), .en(LOAD), .clk(CLOCK), .Q(L4), .clr(RESET));
  Register #(.width(1)) register_6 (.D(I5), .en(LOAD), .clk(CLOCK), .Q(L5), .clr(RESET));
  Register #(.width(1)) register_7 (.D(I6), .en(LOAD), .clk(CLOCK), .Q(L6), .clr(RESET));
  Register #(.width(1)) register_8 (.D(I7), .en(LOAD), .clk(CLOCK), .Q(L7), .clr(RESET));
  assign O6 = ENABLE ? L6 : 1'bz;  // Controlled_Buffer controlled_buffer_1
  assign O7 = ENABLE ? L7 : 1'bz;  // Controlled_Buffer controlled_buffer_2
  assign O2 = ENABLE ? L2 : 1'bz;  // Controlled_Buffer controlled_buffer_3
  assign O3 = ENABLE ? L3 : 1'bz;  // Controlled_Buffer controlled_buffer_4
  assign O4 = ENABLE ? L4 : 1'bz;  // Controlled_Buffer controlled_buffer_5
  assign O5 = ENABLE ? L5 : 1'bz;  // Controlled_Buffer controlled_buffer_6
  assign O0 = ENABLE ? L0 : 1'bz;  // Controlled_Buffer controlled_buffer_7
  assign O1 = ENABLE ? L1 : 1'bz;  // Controlled_Buffer controlled_buffer_8
endmodule

module registro_8bits_test (
  input  in_1,
  input  in_2,
  input  in_3,
  input  in_4,
  input  in_5,
  input  in_6,
  input  in_7,
  input  in_8,
  input  in_9,
  input  RESET,
  input  in_11,
  input  in_12,
  input  in_13,
  input  in_14,
  input  in_15,
  input  in_16,
  input  in_17,
  input  in_18,
  input  in_19,
  input  in_20,
  input  in_21,
  input  in_22,
  input  in_23,
  input  in_24,
  input  in_25,
  input  in_26
);

  wire alu_1_cf, alu_1_l0, alu_1_l1, alu_1_l2, alu_1_l3, alu_1_l4, alu_1_l5, alu_1_l6, alu_1_l7, alu_1_zf,
       CF, clock_1_out, flags_rgister_1_l0, flags_rgister_1_l1, mar_1_o0, mar_1_o1, mar_1_o2, mar_1_o3,
       mar_1_o4, mar_1_o5, mar_1_o6, mar_1_o7, mar_2_o0, mar_2_o1, mar_2_o2, mar_2_o3, program_counter_1_l0,
       program_counter_1_l1, program_counter_1_l2, program_counter_1_l3, program_counter_1_l4,
       program_counter_1_l5, program_counter_1_l6, program_counter_1_l7, registro_8bit_1_l0,
       registro_8bit_1_l1, registro_8bit_1_l2, registro_8bit_1_l3, registro_8bit_1_l4, registro_8bit_1_l5,
       registro_8bit_1_l6, registro_8bit_1_l7, registro_8bit_2_l0, registro_8bit_2_l1, registro_8bit_2_l2,
       registro_8bit_2_l3, registro_8bit_2_l4, registro_8bit_2_l5, registro_8bit_2_l6, registro_8bit_2_l7,
       registro_8bits_b_1_l0, registro_8bits_b_1_l1, registro_8bits_b_1_l2, registro_8bits_b_1_l3,
       registro_8bits_b_1_l4, registro_8bits_b_1_l5, registro_8bits_b_1_l6, registro_8bits_b_1_l7, ZF;
  wire [7:0] controlled_buffer_1_out, mar_1_l0, ram_1_dout;

  Clock clock_1 (.out(clock_1_out));
  RAM ram_1 (
    .addr(mar_1_l0), .we(in_14), .oe(in_16), .clk(clock_1_out), .din(controlled_buffer_1_out),
    .dout(ram_1_dout));
  DotMatrix #(.matrixcols(8), .matrixrows(1)) dotmatrix_1 (
    .col0(mar_1_o7), .col1(mar_1_o6), .col2(mar_1_o5), .col3(mar_1_o4), .col4(mar_1_o3), .col5(mar_1_o2),
    .col6(mar_1_o1), .col7(mar_1_o0));
  MAR mar_1 (
    .ENABLE(1'b1), .I0(controlled_buffer_1_out[0]), .I1(controlled_buffer_1_out[1]),
    .I2(controlled_buffer_1_out[2]), .I3(controlled_buffer_1_out[3]), .I4(controlled_buffer_1_out[4]),
    .I5(controlled_buffer_1_out[5]), .I6(controlled_buffer_1_out[6]), .I7(controlled_buffer_1_out[7]),
    .CLOCK(clock_1_out), .LOAD(in_11), .RESET(RESET), .O0(mar_1_o0), .O1(mar_1_o1), .O2(mar_1_o2),
    .O3(mar_1_o3), .O4(mar_1_o4), .O5(mar_1_o5), .O6(mar_1_o6), .O7(mar_1_o7), .L0(mar_1_l0[0]),
    .L1(mar_1_l0[1]), .L2(mar_1_l0[2]), .L3(mar_1_l0[3]), .L4(mar_1_l0[4]), .L5(mar_1_l0[5]),
    .L6(mar_1_l0[6]), .L7(mar_1_l0[7]));
  MAR mar_2 (
    .ENABLE(in_18), .I0(controlled_buffer_1_out[0]), .I1(controlled_buffer_1_out[1]),
    .I2(controlled_buffer_1_out[2]), .I3(controlled_buffer_1_out[3]), .I4(controlled_buffer_1_out[4]),
    .I5(controlled_buffer_1_out[5]), .I6(controlled_buffer_1_out[6]), .I7(controlled_buffer_1_out[7]),
    .CLOCK(clock_1_out), .LOAD(in_17), .RESET(RESET), .O0(mar_2_o0), .O1(mar_2_o1), .O2(mar_2_o2),
    .O3(mar_2_o3));  // open: O4, O5, O6, O7, L0, L1, L2, L3, L4, L5, L6, L7
  assign controlled_buffer_1_out[0] = in_1 ? in_9 : 1'bz;  // Controlled_Buffer controlled_buffer_1
  assign controlled_buffer_1_out[1] = in_1 ? in_8 : 1'bz;  // Controlled_Buffer controlled_buffer_2
  assign controlled_buffer_1_out[2] = in_1 ? in_7 : 1'bz;  // Controlled_Buffer controlled_buffer_3
  assign controlled_buffer_1_out[3] = in_1 ? in_6 : 1'bz;  // Controlled_Buffer controlled_buffer_4
  assign controlled_buffer_1_out[4] = in_1 ? in_5 : 1'bz;  // Controlled_Buffer controlled_buffer_5
  assign controlled_buffer_1_out[5] = in_1 ? in_4 : 1'bz;  // Controlled_Buffer controlled_buffer_6
  assign controlled_buffer_1_out[6] = in_1 ? in_3 : 1'bz;  // Controlled_Buffer controlled_buffer_7
  assign controlled_buffer_1_out[7] = in_1 ? in_2 : 1'bz;  // Controlled_Buffer controlled_buffer_8
  assign controlled_buffer_1_out[0] = in_16 ? ram_1_dout[0] : 1'bz;  // Controlled_Buffer controlled_buffer_9
  assign controlled_buffer_1_out[1] = in_16 ? ram_1_dout[1] : 1'bz;  // Controlled_Buffer controlled_buffer_10
  assign controlled_buffer_1_out[2] = in_16 ? ram_1_dout[2] : 1'bz;  // Controlled_Buffer controlled_buffer_11
  assign controlled_buffer_1_out[3] = in_16 ? ram_1_dout[3] : 1'bz;  // Controlled_Buffer controlled_buffer_12
  assign controlled_buffer_1_out[4] = in_16 ? ram_1_dout[4] : 1'bz;  // Controlled_Buffer controlled_buffer_13
  assign controlled_buffer_1_out[5] = in_16 ? ram_1_dout[5] : 1'bz;  // Controlled_Buffer controlled_buffer_14
  assign controlled_buffer_1_out[6] = in_16 ? ram_1_dout[6] : 1'bz;  // Controlled_Buffer controlled_buffer_15
  assign controlled_buffer_1_out[7] = in_16 ? ram_1_dout[7] : 1'bz;  // Controlled_Buffer controlled_buffer_16
  DotMatrix #(.matrixcols(8), .matrixrows(1)) dotmatrix_2 (
    .col0(controlled_buffer_1_out[7]), .col1(controlled_buffer_1_out[6]), .col2(controlled_buffer_1_out[5]),
    .col3(controlled_buffer_1_out[4]), .col4(controlled_buffer_1_out[3]), .col5(controlled_buffer_1_out[2]),
    .col6(controlled_buffer_1_out[1]), .col7(controlled_buffer_1_out[0]));
  PROGRAM_COUNTER program_counter_1 (
    .COut(in_12), .CEnable(in_15), .CWrite(in_13), .CReset(RESET), .CLOCK(clock_1_out),
    .I7(controlled_buffer_1_out[7]), .I6(controlled_buffer_1_out[6]), .I5(controlled_buffer_1_out[5]),
    .I4(controlled_buffer_1_out[4]), .I3(controlled_buffer_1_out[3]), .I2(controlled_buffer_1_out[2]),
    .I1(controlled_buffer_1_out[1]), .I0(controlled_buffer_1_out[0]), .O7(controlled_buffer_1_out[7]),
    .O6(controlled_buffer_1_out[6]), .O5(controlled_buffer_1_out[5]), .O4(controlled_buffer_1_out[4]),
    .O3(controlled_buffer_1_out[3]), .O2(controlled_buffer_1_out[2]), .O1(controlled_buffer_1_out[1]),
    .O0(controlled_buffer_1_out[0]), .L7(program_counter_1_l7), .L6(program_counter_1_l6),
    .L5(program_counter_1_l5), .L4(program_counter_1_l4), .L3(program_counter_1_l3),
    .L2(program_counter_1_l2), .L1(program_counter_1_l1), .L0(program_counter_1_l0));
  DotMatrix #(.matrixcols(8), .matrixrows(1)) dotmatrix_3 (
    .col0(registro_8bit_2_l0), .col1(registro_8bit_2_l1), .col2(registro_8bit_2_l2),
    .col3(registro_8bit_2_l3), .col4(registro_8bit_2_l4), .col5(registro_8bit_2_l5),
    .col6(registro_8bit_2_l6), .col7(registro_8bit_2_l7));
  DotMatrix #(.matrixcols(8), .matrixrows(1)) dotmatrix_4 (
    .col0(registro_8bits_b_1_l0), .col1(registro_8bits_b_1_l1), .col2(registro_8bits_b_1_l2),
    .col3(registro_8bits_b_1_l3), .col4(registro_8bits_b_1_l4), .col5(registro_8bits_b_1_l5),
    .col6(registro_8bits_b_1_l6), .col7(registro_8bits_b_1_l7));
  DotMatrix #(.matrixcols(8), .matrixrows(1)) dotmatrix_5 (
    .col0(registro_8bit_1_l0), .col1(registro_8bit_1_l1), .col2(registro_8bit_1_l2),
    .col3(registro_8bit_1_l3), .col4(registro_8bit_1_l4), .col5(registro_8bit_1_l5),
    .col6(registro_8bit_1_l6), .col7(registro_8bit_1_l7));
  registro_8bit registro_8bit_1 (
    .I0(controlled_buffer_1_out[0]), .I1(controlled_buffer_1_out[1]), .I2(controlled_buffer_1_out[2]),
    .I3(controlled_buffer_1_out[3]), .I4(controlled_buffer_1_out[4]), .I5(controlled_buffer_1_out[5]),
    .I6(controlled_buffer_1_out[6]), .I7(controlled_buffer_1_out[7]), .CLOCK(clock_1_out), .LOAD(in_20),
    .RESET(RESET), .L0(registro_8bit_1_l0), .L1(registro_8bit_1_l1), .L2(registro_8bit_1_l2),
    .L3(registro_8bit_1_l3), .L4(registro_8bit_1_l4), .L5(registro_8bit_1_l5), .L6(registro_8bit_1_l6),
    .L7(registro_8bit_1_l7));  // open: ENABLE, O0, O1, O2, O3, O4, O5, O6, O7
  DotMatrix #(.matrixcols(8), .matrixrows(1)) dotmatrix_6 (
    .col0(program_counter_1_l0), .col1(program_counter_1_l1), .col2(program_counter_1_l2),
    .col3(program_counter_1_l3), .col4(program_counter_1_l4), .col5(program_counter_1_l5),
    .col6(program_counter_1_l6), .col7(program_counter_1_l7));
  registro_8bit registro_8bit_2 (
    .ENABLE(in_25), .I0(controlled_buffer_1_out[0]), .I1(controlled_buffer_1_out[1]),
    .I2(controlled_buffer_1_out[2]), .I3(controlled_buffer_1_out[3]), .I4(controlled_buffer_1_out[4]),
    .I5(controlled_buffer_1_out[5]), .I6(controlled_buffer_1_out[6]), .I7(controlled_buffer_1_out[7]),
    .CLOCK(clock_1_out), .LOAD(in_23), .RESET(RESET), .O0(controlled_buffer_1_out[0]),
    .O1(controlled_buffer_1_out[1]), .O2(controlled_buffer_1_out[2]), .O3(controlled_buffer_1_out[3]),
    .O4(controlled_buffer_1_out[4]), .O5(controlled_buffer_1_out[5]), .O6(controlled_buffer_1_out[6]),
    .O7(controlled_buffer_1_out[7]), .L0(registro_8bit_2_l0), .L1(registro_8bit_2_l1),
    .L2(registro_8bit_2_l2), .L3(registro_8bit_2_l3), .L4(registro_8bit_2_l4), .L5(registro_8bit_2_l5),
    .L6(registro_8bit_2_l6), .L7(registro_8bit_2_l7));
  registro_8bits_B registro_8bits_b_1 (
    .ENABLE(in_24), .I0(controlled_buffer_1_out[0]), .I1(controlled_buffer_1_out[1]),
    .I2(controlled_buffer_1_out[2]), .I3(controlled_buffer_1_out[3]), .I4(controlled_buffer_1_out[4]),
    .I5(controlled_buffer_1_out[5]), .I6(controlled_buffer_1_out[6]), .I7(controlled_buffer_1_out[7]),
    .CLOCK(clock_1_out), .LOAD(in_22), .RESET(RESET), .O0(controlled_buffer_1_out[0]),
    .O1(controlled_buffer_1_out[1]), .O2(controlled_buffer_1_out[2]), .O3(controlled_buffer_1_out[3]),
    .O4(controlled_buffer_1_out[4]), .O5(controlled_buffer_1_out[5]), .O6(controlled_buffer_1_out[6]),
    .O7(controlled_buffer_1_out[7]), .L0(registro_8bits_b_1_l0), .L1(registro_8bits_b_1_l1),
    .L2(registro_8bits_b_1_l2), .L3(registro_8bits_b_1_l3), .L4(registro_8bits_b_1_l4),
    .L5(registro_8bits_b_1_l5), .L6(registro_8bits_b_1_l6), .L7(registro_8bits_b_1_l7));
  DotMatrix #(.matrixcols(8), .matrixrows(1)) dotmatrix_7 (
    .col0(alu_1_l0), .col1(alu_1_l1), .col2(alu_1_l2), .col3(alu_1_l3), .col4(alu_1_l4), .col5(alu_1_l5),
    .col6(alu_1_l6), .col7(alu_1_l7));
  ALU alu_1 (
    .ENABLE(in_21), .A7(registro_8bit_2_l7), .B7(registro_8bits_b_1_l7), .A6(registro_8bit_2_l6),
    .B6(registro_8bits_b_1_l6), .A5(registro_8bit_2_l5), .B5(registro_8bits_b_1_l5), .A4(registro_8bit_2_l4),
    .B4(registro_8bits_b_1_l4), .A3(registro_8bit_2_l3), .B3(registro_8bits_b_1_l3), .A2(registro_8bit_2_l2),
    .B2(registro_8bits_b_1_l2), .A1(registro_8bit_2_l1), .B1(registro_8bits_b_1_l1), .A0(registro_8bit_2_l0),
    .B0(registro_8bits_b_1_l0), .su(in_19), .E0(controlled_buffer_1_out[0]), .E1(controlled_buffer_1_out[1]),
    .E2(controlled_buffer_1_out[2]), .E3(controlled_buffer_1_out[3]), .E4(controlled_buffer_1_out[4]),
    .E5(controlled_buffer_1_out[5]), .E6(controlled_buffer_1_out[6]), .E7(controlled_buffer_1_out[7]),
    .CF(alu_1_cf), .ZF(alu_1_zf), .L7(alu_1_l7), .L6(alu_1_l6), .L5(alu_1_l5), .L4(alu_1_l4), .L3(alu_1_l3),
    .L2(alu_1_l2), .L1(alu_1_l1), .L0(alu_1_l0));
  DotMatrix #(.matrixcols(2), .matrixrows(1)) dotmatrix_8 (.col0(flags_rgister_1_l0), .col1(flags_rgister_1_l1));
  flags_rgister flags_rgister_1 (
    .I0(alu_1_cf), .I1(alu_1_zf), .CLOCK(clock_1_out), .LOAD(in_26), .RESET(RESET), .ENABLE(1'b1),
    .L0(flags_rgister_1_l0), .L1(flags_rgister_1_l1), .O0(CF), .O1(ZF));

  // Other names for the same wires on the sheet: AI = in_23; AO = in_25; BI = in_22; BO = in_24; CE = in_15;
  //   CO = in_12; EO = in_21; FI = in_26; II = in_17; IO = in_18; JM = in_13; MI = in_11; OI = in_20; RI = in_14;
  //   RO = in_16; SU = in_19

  // Notes on the sheet:
  //   MAR
  //   IR
  //   PC
  //   8bits-register-A
  //   OutPut-register
endmodule

module ALU (
  input  ENABLE,
  input  su,
  input  A7,
  input  A6,
  input  A5,
  input  A4,
  input  A3,
  input  A2,
  input  A1,
  input  A0,
  input  B7,
  input  B6,
  input  B5,
  input  B4,
  input  B3,
  input  B2,
  input  B1,
  input  B0,
  output L7,
  output L6,
  output L5,
  output L4,
  output L3,
  output L2,
  output L1,
  output L0,
  output E0,
  output CF,
  output ZF,
  output E1,
  output E2,
  output E3,
  output E4,
  output E5,
  output E6,
  output E7
);

  wire [7:0] xor_8_out;

  xor xor_1 (xor_8_out[7], B7, su);
  xor xor_2 (xor_8_out[6], B6, su);
  xor xor_3 (xor_8_out[5], B5, su);
  Adder adder_1 (
    .a({A7, A6, A5, A4, A3, A2, A1, A0}), .b(xor_8_out), .out({L7, L6, L5, L4, L3, L2, L1, L0}), .cin(su),
    .cout(CF));
  xor xor_4 (xor_8_out[4], B4, su);
  xor xor_5 (xor_8_out[3], B3, su);
  xor xor_6 (xor_8_out[2], B2, su);
  xor xor_7 (xor_8_out[1], B1, su);
  xor xor_8 (xor_8_out[0], B0, su);
  nor nor_1 (ZF, L0, L1, L2, L3, L4, L5, L6, L7);
  assign E0 = ENABLE ? L0 : 1'bz;  // Controlled_Buffer controlled_buffer_1
  assign E1 = ENABLE ? L1 : 1'bz;  // Controlled_Buffer controlled_buffer_2
  assign E2 = ENABLE ? L2 : 1'bz;  // Controlled_Buffer controlled_buffer_3
  assign E3 = ENABLE ? L3 : 1'bz;  // Controlled_Buffer controlled_buffer_4
  assign E4 = ENABLE ? L4 : 1'bz;  // Controlled_Buffer controlled_buffer_5
  assign E5 = ENABLE ? L5 : 1'bz;  // Controlled_Buffer controlled_buffer_6
  assign E6 = ENABLE ? L6 : 1'bz;  // Controlled_Buffer controlled_buffer_7
  assign E7 = ENABLE ? L7 : 1'bz;  // Controlled_Buffer controlled_buffer_8
endmodule

module registro_8bits_B (
  input  CLOCK,
  input  LOAD,
  input  RESET,
  input  ENABLE,
  input  I0,
  input  I1,
  input  I2,
  input  I3,
  input  I4,
  input  I5,
  input  I6,
  input  I7,
  output L0,
  output L1,
  output L2,
  output L3,
  output L4,
  output L5,
  output L6,
  output L7,
  output O0,
  output O1,
  output O2,
  output O3,
  output O4,
  output O5,
  output O6,
  output O7
);

  Register #(.width(1)) register_1 (.D(I0), .en(LOAD), .clk(CLOCK), .Q(L0), .clr(RESET));
  Register #(.width(1)) register_2 (.D(I1), .en(LOAD), .clk(CLOCK), .Q(L1), .clr(RESET));
  Register #(.width(1)) register_3 (.D(I2), .en(LOAD), .clk(CLOCK), .Q(L2), .clr(RESET));
  Register #(.width(1)) register_4 (.D(I3), .en(LOAD), .clk(CLOCK), .Q(L3), .clr(RESET));
  Register #(.width(1)) register_5 (.D(I4), .en(LOAD), .clk(CLOCK), .Q(L4), .clr(RESET));
  Register #(.width(1)) register_6 (.D(I5), .en(LOAD), .clk(CLOCK), .Q(L5), .clr(RESET));
  Register #(.width(1)) register_7 (.D(I6), .en(LOAD), .clk(CLOCK), .Q(L6), .clr(RESET));
  Register #(.width(1)) register_8 (.D(I7), .en(LOAD), .clk(CLOCK), .Q(L7), .clr(RESET));
  assign O6 = ENABLE ? L6 : 1'bz;  // Controlled_Buffer controlled_buffer_1
  assign O7 = ENABLE ? L7 : 1'bz;  // Controlled_Buffer controlled_buffer_2
  assign O2 = ENABLE ? L2 : 1'bz;  // Controlled_Buffer controlled_buffer_3
  assign O3 = ENABLE ? L3 : 1'bz;  // Controlled_Buffer controlled_buffer_4
  assign O4 = ENABLE ? L4 : 1'bz;  // Controlled_Buffer controlled_buffer_5
  assign O5 = ENABLE ? L5 : 1'bz;  // Controlled_Buffer controlled_buffer_6
  assign O0 = ENABLE ? L0 : 1'bz;  // Controlled_Buffer controlled_buffer_7
  assign O1 = ENABLE ? L1 : 1'bz;  // Controlled_Buffer controlled_buffer_8
endmodule

module MAR (
  input  CLOCK,
  input  LOAD,
  input  RESET,
  input  ENABLE,
  input  I0,
  input  I1,
  input  I2,
  input  I3,
  input  I4,
  input  I5,
  input  I6,
  input  I7,
  output L0,
  output L1,
  output L2,
  output L3,
  output L4,
  output L5,
  output L6,
  output L7,
  output O0,
  output O1,
  output O2,
  output O3,
  output O4,
  output O5,
  output O6,
  output O7
);

  Register #(.width(1)) register_1 (.D(I0), .en(LOAD), .clk(CLOCK), .Q(L0), .clr(RESET));
  Register #(.width(1)) register_2 (.D(I1), .en(LOAD), .clk(CLOCK), .Q(L1), .clr(RESET));
  Register #(.width(1)) register_3 (.D(I2), .en(LOAD), .clk(CLOCK), .Q(L2), .clr(RESET));
  Register #(.width(1)) register_4 (.D(I3), .en(LOAD), .clk(CLOCK), .Q(L3), .clr(RESET));
  Register #(.width(1)) register_5 (.D(I4), .en(LOAD), .clk(CLOCK), .Q(L4), .clr(RESET));
  Register #(.width(1)) register_6 (.D(I5), .en(LOAD), .clk(CLOCK), .Q(L5), .clr(RESET));
  Register #(.width(1)) register_7 (.D(I6), .en(LOAD), .clk(CLOCK), .Q(L6), .clr(RESET));
  Register #(.width(1)) register_8 (.D(I7), .en(LOAD), .clk(CLOCK), .Q(L7), .clr(RESET));
  assign O6 = ENABLE ? L6 : 1'bz;  // Controlled_Buffer controlled_buffer_1
  assign O7 = ENABLE ? L7 : 1'bz;  // Controlled_Buffer controlled_buffer_2
  assign O2 = ENABLE ? L2 : 1'bz;  // Controlled_Buffer controlled_buffer_3
  assign O3 = ENABLE ? L3 : 1'bz;  // Controlled_Buffer controlled_buffer_4
  assign O4 = ENABLE ? L4 : 1'bz;  // Controlled_Buffer controlled_buffer_5
  assign O5 = ENABLE ? L5 : 1'bz;  // Controlled_Buffer controlled_buffer_6
  assign O0 = ENABLE ? L0 : 1'bz;  // Controlled_Buffer controlled_buffer_7
  assign O1 = ENABLE ? L1 : 1'bz;  // Controlled_Buffer controlled_buffer_8
endmodule

module PROGRAM_COUNTER (
  input  COut,
  input  CEnable,
  input  CWrite,
  input  CReset,
  input  CLOCK,
  input  I7,
  input  I6,
  input  I5,
  input  I4,
  input  I3,
  input  I2,
  input  I1,
  input  I0,
  output O7,
  output O6,
  output O5,
  output O4,
  output O3,
  output O2,
  output O1,
  output O0,
  output L7,
  output L6,
  output L5,
  output L4,
  output L3,
  output L2,
  output L1,
  output L0
);

  wire and_1_out, and_2_out, and_3_out, and_4_out, and_5_out, and_6_out, and_7_out, and_8_out, and_9_out,
       and_10_out, and_11_out, and_12_out, and_13_out, and_14_out, and_15_out, and_16_out, j_k_ff_2_qn,
       j_k_ff_3_qn, j_k_ff_4_qn, j_k_ff_5_qn, j_k_ff_6_qn, j_k_ff_7_qn, j_k_ff_8_qn, or_1_out, or_2_out,
       or_3_out, or_4_out, or_5_out, or_6_out, or_7_out, or_8_out;

  J_K_Flip_Flop j_k_ff_1 (
    .J(CEnable), .K(CEnable), .clk(j_k_ff_2_qn), .Q(L7), .preset(and_1_out), .reset(or_1_out));  // open: Qn
  or or_1 (or_1_out, CReset, and_2_out);
  and and_1 (and_1_out, CWrite, I7, CLOCK);
  and and_2 (and_2_out, CWrite, ~I7, CLOCK);  // AND_Gate
  J_K_Flip_Flop j_k_ff_2 (
    .J(CEnable), .K(CEnable), .clk(j_k_ff_3_qn), .Q(L6), .Qn(j_k_ff_2_qn), .preset(and_3_out),
    .reset(or_2_out));
  or or_2 (or_2_out, CReset, and_4_out);
  and and_3 (and_3_out, CWrite, I6, CLOCK);
  and and_4 (and_4_out, CWrite, ~I6, CLOCK);  // AND_Gate
  assign O7 = COut ? L7 : 1'bz;  // Controlled_Buffer controlled_buffer_1
  assign O6 = COut ? L6 : 1'bz;  // Controlled_Buffer controlled_buffer_2
  J_K_Flip_Flop j_k_ff_3 (
    .J(CEnable), .K(CEnable), .clk(j_k_ff_4_qn), .Q(L5), .Qn(j_k_ff_3_qn), .preset(and_5_out),
    .reset(or_3_out));
  or or_3 (or_3_out, CReset, and_6_out);
  and and_5 (and_5_out, CWrite, I5, CLOCK);
  and and_6 (and_6_out, CWrite, ~I5, CLOCK);  // AND_Gate
  assign O5 = COut ? L5 : 1'bz;  // Controlled_Buffer controlled_buffer_3
  assign O4 = COut ? L4 : 1'bz;  // Controlled_Buffer controlled_buffer_4
  assign O3 = COut ? L3 : 1'bz;  // Controlled_Buffer controlled_buffer_5
  assign O2 = COut ? L2 : 1'bz;  // Controlled_Buffer controlled_buffer_6
  J_K_Flip_Flop j_k_ff_4 (
    .J(CEnable), .K(CEnable), .clk(j_k_ff_5_qn), .Q(L4), .Qn(j_k_ff_4_qn), .preset(and_7_out),
    .reset(or_4_out));
  or or_4 (or_4_out, CReset, and_8_out);
  and and_7 (and_7_out, CWrite, I4, CLOCK);
  and and_8 (and_8_out, CWrite, ~I4, CLOCK);  // AND_Gate
  assign O1 = COut ? L1 : 1'bz;  // Controlled_Buffer controlled_buffer_7
  assign O0 = COut ? L0 : 1'bz;  // Controlled_Buffer controlled_buffer_8
  J_K_Flip_Flop j_k_ff_5 (
    .J(CEnable), .K(CEnable), .clk(j_k_ff_6_qn), .Q(L3), .Qn(j_k_ff_5_qn), .preset(and_9_out),
    .reset(or_5_out));
  or or_5 (or_5_out, CReset, and_10_out);
  and and_9 (and_9_out, CWrite, I3, CLOCK);
  J_K_Flip_Flop j_k_ff_6 (
    .J(CEnable), .K(CEnable), .clk(j_k_ff_7_qn), .Q(L2), .Qn(j_k_ff_6_qn), .preset(and_11_out),
    .reset(or_6_out));
  and and_10 (and_10_out, CWrite, ~I3, CLOCK);  // AND_Gate
  and and_11 (and_11_out, CWrite, I2, CLOCK);
  J_K_Flip_Flop j_k_ff_7 (
    .J(CEnable), .K(CEnable), .clk(j_k_ff_8_qn), .Q(L1), .Qn(j_k_ff_7_qn), .preset(and_13_out),
    .reset(or_7_out));
  or or_6 (or_6_out, CReset, and_12_out);
  and and_12 (and_12_out, CWrite, ~I2, CLOCK);  // AND_Gate
  and and_13 (and_13_out, CWrite, I1, CLOCK);
  or or_7 (or_7_out, CReset, and_15_out);
  and and_14 (and_14_out, CWrite, I0, CLOCK);
  and and_15 (and_15_out, CWrite, ~I1, CLOCK);  // AND_Gate
  J_K_Flip_Flop j_k_ff_8 (
    .J(CEnable), .K(CEnable), .clk(CLOCK), .Q(L0), .Qn(j_k_ff_8_qn), .preset(and_14_out), .reset(or_8_out));
  or or_8 (or_8_out, CReset, and_16_out);
  and and_16 (and_16_out, CWrite, ~I0, CLOCK);  // AND_Gate
endmodule

module flags_rgister (
  input  CLOCK,
  input  LOAD,
  input  RESET,
  input  ENABLE,
  input  I0,
  input  I1,
  output L0,
  output L1,
  output O0,
  output O1
);

  Register #(.width(1)) register_1 (.D(I0), .en(LOAD), .clk(CLOCK), .Q(L0), .clr(RESET));
  Register #(.width(1)) register_2 (.D(I1), .en(LOAD), .clk(CLOCK), .Q(L1), .clr(RESET));
  assign O0 = ENABLE ? L0 : 1'bz;  // Controlled_Buffer controlled_buffer_1
  assign O1 = ENABLE ? L1 : 1'bz;  // Controlled_Buffer controlled_buffer_2
endmodule

module INSTRUCCION_DECODER (
  input  ZF,
  input  CF,
  input  OP0,
  input  OP1,
  input  OP2,
  input  OP3,
  input  OP4,
  input  COLCK,
  input  CLEAR
);

  wire clock_1_out, decoder_4bits_1_d0, decoder_4bits_1_d1, decoder_4bits_1_d2, decoder_4bits_1_d3,
       decoder_4bits_1_d4, decoder_4bits_1_d5, decoder_4bits_1_d6, decoder_4bits_1_d7, decoder_4bits_1_d8,
       not_1_out, or_1_out, program_counter_1_l3;
  wire [2:0] program_counter_1_l0;

  Clock clock_1 (.out(clock_1_out));
  not not_1 (not_1_out, clock_1_out);
  or or_1 (or_1_out, CLEAR, decoder_4bits_1_d8);
  PROGRAM_COUNTER program_counter_1 (
    .CEnable(not_1_out), .CReset(or_1_out), .CLOCK(not_1_out), .L3(program_counter_1_l3),
    .L2(program_counter_1_l0[2]), .L1(program_counter_1_l0[1]), .L0(program_counter_1_l0[0]));  // open: COut, CWrite, I7, I6, I5, I4, I3, I2, I1, I0, O7, O6, O5, O4, O3, O2, O1, O0, L7, L6, L5, L4
  // NOT_Gate not_2 has open pins: in=COLCK, out=open
  decoder_4bits decoder_4bits_1 (
    .I4(program_counter_1_l3), .I2(program_counter_1_l0[2]), .I1(program_counter_1_l0[1]),
    .I0(program_counter_1_l0[0]), .ENABLE(1'b1), .D8(decoder_4bits_1_d8), .D7(decoder_4bits_1_d7),
    .D6(decoder_4bits_1_d6), .D5(decoder_4bits_1_d5), .D4(decoder_4bits_1_d4), .D3(decoder_4bits_1_d3),
    .D2(decoder_4bits_1_d2), .D1(decoder_4bits_1_d1), .D0(decoder_4bits_1_d0));  // open: DF, DE, DD, DC, DB, DA, D9
  LED S0 (.in(decoder_4bits_1_d0));
  LED S1 (.in(decoder_4bits_1_d1));
  LED S2 (.in(decoder_4bits_1_d2));
  ROM #(.addrWidth(10), .dataWidth(17)) rom_1 (.addr({OP4, OP3, OP2, OP1, OP0, CF, ZF, program_counter_1_l0}));  // open: data
  LED S3 (.in(decoder_4bits_1_d3));
  LED S4 (.in(decoder_4bits_1_d4));
  LED S5 (.in(decoder_4bits_1_d5));
  LED S6 (.in(decoder_4bits_1_d6));
  LED S7 (.in(decoder_4bits_1_d7));

  // Notes on the sheet:
  //   counter
endmodule

module decoder_4bits (
  input  ENABLE,
  input  I4,
  input  I2,
  input  I1,
  input  I0,
  output DF,
  output DE,
  output DD,
  output DC,
  output DB,
  output DA,
  output D9,
  output D8,
  output D7,
  output D6,
  output D5,
  output D4,
  output D3,
  output D2,
  output D1,
  output D0
);

  wire and_1_out, and_2_out, and_3_out, and_4_out, and_5_out, and_6_out, and_7_out, and_8_out, and_9_out,
       and_10_out, and_11_out, and_12_out, and_13_out, and_14_out, and_15_out, and_16_out, not_1_out,
       not_2_out, not_3_out, not_4_out;

  not not_1 (not_1_out, I4);
  not not_2 (not_2_out, I2);
  not not_3 (not_3_out, I1);
  not not_4 (not_4_out, I0);
  and and_1 (and_1_out, not_1_out, not_2_out, not_3_out, not_4_out);
  and and_2 (and_2_out, not_1_out, not_2_out, not_3_out, I0);
  and and_3 (and_3_out, not_1_out, not_2_out, I1, not_4_out);
  and and_4 (and_4_out, not_1_out, not_2_out, I1, I0);
  and and_5 (and_5_out, not_1_out, I2, not_3_out, not_4_out);
  and and_6 (and_6_out, not_1_out, I2, not_3_out, I0);
  and and_7 (and_7_out, not_1_out, I2, I1, not_4_out);
  and and_8 (and_8_out, not_1_out, I2, I1, I0);
  and and_9 (and_9_out, I4, not_2_out, not_3_out, not_4_out);
  and and_10 (and_10_out, I4, not_2_out, not_3_out, I0);
  and and_11 (and_11_out, I4, not_2_out, I1, not_4_out);
  and and_12 (and_12_out, I4, not_2_out, I1, I0);
  and and_13 (and_13_out, I4, I2, not_3_out, not_4_out);
  and and_14 (and_14_out, I4, I2, not_3_out, I0);
  and and_15 (and_15_out, I4, I2, I1, not_4_out);
  and and_16 (and_16_out, I4, I2, I1, I0);
  assign DF = ENABLE ? and_16_out : 1'bz;  // Controlled_Buffer controlled_buffer_1
  assign DE = ENABLE ? and_15_out : 1'bz;  // Controlled_Buffer controlled_buffer_2
  assign DD = ENABLE ? and_14_out : 1'bz;  // Controlled_Buffer controlled_buffer_3
  assign DC = ENABLE ? and_13_out : 1'bz;  // Controlled_Buffer controlled_buffer_4
  assign DB = ENABLE ? and_12_out : 1'bz;  // Controlled_Buffer controlled_buffer_5
  assign DA = ENABLE ? and_11_out : 1'bz;  // Controlled_Buffer controlled_buffer_6
  assign D9 = ENABLE ? and_10_out : 1'bz;  // Controlled_Buffer controlled_buffer_7
  assign D8 = ENABLE ? and_9_out : 1'bz;  // Controlled_Buffer controlled_buffer_8
  assign D7 = ENABLE ? and_8_out : 1'bz;  // Controlled_Buffer controlled_buffer_9
  assign D6 = ENABLE ? and_7_out : 1'bz;  // Controlled_Buffer controlled_buffer_10
  assign D5 = ENABLE ? and_6_out : 1'bz;  // Controlled_Buffer controlled_buffer_11
  assign D4 = ENABLE ? and_5_out : 1'bz;  // Controlled_Buffer controlled_buffer_12
  assign D3 = ENABLE ? and_4_out : 1'bz;  // Controlled_Buffer controlled_buffer_13
  assign D2 = ENABLE ? and_3_out : 1'bz;  // Controlled_Buffer controlled_buffer_14
  assign D1 = ENABLE ? and_2_out : 1'bz;  // Controlled_Buffer controlled_buffer_15
  assign D0 = ENABLE ? and_1_out : 1'bz;  // Controlled_Buffer controlled_buffer_16
endmodule
